// Logisim project lab_3.circ as structural Verilog: 1 circuit, main circuit main
module main (
  input  in_1,
  input  in_2,
  input  in_3,
  input  in_4,
  input  in_5,
  input  in_6,
  input  in_7,
  input  in_8,
  input  in_9,
  input  in_10,
  output out_11,
  output out_12,
  output out_13,
  output out_14
);

  wire and_1_out, and_3_out, and_4_out, not_1_out, not_2_out, not_3_out, or_1_out, or_2_out, or_3_out;

  not not_1 (not_1_out, in_6);
  not not_2 (not_2_out, in_8);
  or or_1 (or_1_out, in_9, in_10);
  and and_1 (and_1_out, in_1, in_2);
  or or_2 (or_2_out, in_3, in_4);
  or or_3 (or_3_out, not_1_out, in_7);
  and and_2 (out_14, in_8, or_1_out);
  not not_3 (not_3_out, and_3_out);
  and and_3 (and_3_out, or_2_out, in_5);
  and and_4 (and_4_out, or_3_out, not_2_out);
  not not_4 (out_12, out_13);
  or or_4 (out_13, and_4_out, out_14);
  and and_5 (out_11, and_1_out, not_3_out);
endmodule
