// Logisim project lab_5.circ as structural Verilog: 2 circuits, main circuit D-триггер
module \D_триггер  (
  input  D,
  input  C,
  output out_3,
  output out_4
);

  wire nand_1_out, nand_2_out;

  nand nand_1 (nand_1_out, D, C);
  nand nand_2 (nand_2_out, nand_1_out, C);
  nand nand_3 (out_3, nand_1_out, out_4);
  nand nand_4 (out_4, out_3, nand_2_out);
endmodule

module \Т_триггер  (
  input  \Т ,
  input  \С ,
  output out_3,
  output out_4
);

  wire and_1_out, d_ff_1_q, d_ff_1_qn, d_ff_2_qn, nand_1_out;

  nand nand_1 (nand_1_out, \Т , \С );
  D_Flip_Flop d_ff_1 (.clk(out_4), .D(and_1_out), .Q(d_ff_1_q), .Qn(d_ff_1_qn));  // open: preset, en, reset
  and and_1 (and_1_out, d_ff_1_qn, nand_1_out);
  D_Flip_Flop d_ff_2 (.clk(d_ff_1_q), .D(out_4), .Q(out_3), .Qn(d_ff_2_qn));  // open: preset, en, reset
  nand nand_2 (out_4, d_ff_2_qn, nand_1_out);
endmodule
